# Fritzing sketch MainSCH (saved by Fritzing 1.0.3b)
breadboards: 1

parts:
  Controller = Arduino Uno (Rev3)
  Temperature_Sensor = TMP36 [package=to-92]
  R1 = Resistor [tolerance=±5% power=0.25W resistance=470 package=THT]
  Part1 = Soil Moisture Sensor
  SolarCell = S1133 Si Photodiode [package="8mm Ceramic [THT]"]
  WaterPump = DC Motor [voltage_(max)=6V voltage_(min)=3V]
  pumpSwithcTR = NPN-Transistor [package="TO92 [THT]"]

nets:
  N1: Controller.A0, Part1.SIG
  N2: Controller.A1, SolarCell.cathode
  N3: Controller.A3, pumpSwithcTR.B
  GND: Controller.GND, Temperature_Sensor.GND, Part1.GND, SolarCell.anode, pumpSwithcTR.E
  N4: Controller.D4, R1.Pin_1
  12V: Controller.VIN, WaterPump.pin_1
  5V: Temperature_Sensor.VCC, Part1.VCC
  N5: Temperature_Sensor.VOUT, R1.Pin_0
  N6: WaterPump.pin_2, pumpSwithcTR.C
